# Fritzing sketch pico_thermostat (saved by Fritzing 1.0.1rc)
breadboards: 1

parts:
  A1 = Raspberry Pi Pico H
  OLED1 = OLED 128x64 I2C Monochrome Display
  Q1 = TRANSISTOR_NPN [package=to-92-ammo]
  R1 = Resistor [tolerance=±5% resistance=220 package="0805 [SMD]"]
  F1 = Small Fan, based on Fan - Ventilador [package=THT]
  J1 = 2.1mm Barrel Jack with Terminal Block
  DHT1 = DHT11 Humitidy and Temperature Sensor

nets:
  N1: A1.GND, DHT1.NULL
  N2: A1.GP9, R1.Pin_0
  N3: A1.GP12, DHT1.DATA
  N4: A1.GP13, DHT1.GND
  N5: A1.GP18, OLED1.SDA
  N6: A1.GP19, OLED1.SCK
  VDD: A1.VBUS, OLED1.VDD, DHT1.VDD
  N7: OLED1.GND, Q1.E
  N8: Q1.B, R1.Pin_1
  N9: F1.5V, J1.POS

custom parts:
  Raspberry Pi Pico H: Raspberry Pi Pico H. Based around the RP2040 microcontroller the Pico H is a low cost microcontroller device bringing Raspberry Pi quality, cost, and easy of use to the microcontroller space.
  Small Fan, based on Fan - Ventilador: Small 2-pin fan, commonly used with single-board computers, 3d-printers, etc. This work is based on a much larger fan, as commonly found in desktop computers
  DHT11 Humitidy and Temperature Sensor: DHT11 Humidity and Temperature Sensor
